# Fritzing sketch LD293 (saved by Fritzing 0.9.3b)
breadboards: 1

parts:
  IC1 = L293D [package=THT]
  VCC1 = Battery
  M1 = DC Motor
  M2 = DC Motor
  S1 = Pushbutton [package="[THT]"]
  S2 = Pushbutton [package="[THT]"]
  R1 = Resistor [tolerance=±5% resistance=10k package=THT]
  VCC2 = Battery block 9V
  R2 = Resistor [tolerance=±5% resistance=10k package=THT]
  S5 = Pushbutton [package="[THT]"]
  S6 = Pushbutton [package="[THT]"]
  R5 = Resistor [tolerance=±5% resistance=10k package=THT]
  R6 = Resistor [tolerance=±5% resistance=10k package=THT]

nets:
  N1: IC1.Enable_1, IC1.Enable_2, IC1.+V, VCC1.+, S1.Pin_3, S1.Pin_4, S2.Pin_3, S2.Pin_4, S5.Pin_1, S5.Pin_2, S6.Pin_1, S6.Pin_2
  N2: IC1.In_1, S1.Pin_1, S1.Pin_2, R1.Pin_0
  N3: IC1.Out_1_(_Controlled_by_Enable_1_), M1.pin_2
  N4: IC1.0V, VCC1.-, R1.Pin_1, VCC2.-, R2.Pin_1, R5.Pin_0, R6.Pin_0
  N5: IC1.Out_2_(_Controlled_by_Enable_1_), M1.pin_1
  N6: IC1.In_2, S2.Pin_1, S2.Pin_2, R2.Pin_0
  N7: IC1.+Vmotor, VCC2.+
  N8: IC1.In_3, S5.Pin_3, S5.Pin_4, R5.Pin_1
  N9: IC1.Out_3_(_Controlled_by_Enable_2_), M2.pin_2
  N10: IC1.Out_4_(_Controlled_by_Enable_2_), M2.pin_1
  N11: IC1.In_4, S6.Pin_3, S6.Pin_4, R6.Pin_1
